# Fritzing sketch schematics-mini (saved by Fritzing 1.0.5)

parts:
  A1 = ESP32-S3-WROOM-1-N16R8 dev board
  Componente1 = LIPO-2200mAh
  M1 = DC Motor [voltage_(max)=6V voltage_(min)=3V]  # not connected
  M2 = DC Motor [voltage_(max)=6V voltage_(min)=3V]  # not connected
  M3 = DC Motor [voltage_(max)=6V voltage_(min)=3V]  # not connected
  M5 = DC Motor [voltage_(max)=6V voltage_(min)=3V]  # not connected
  M7 = DC Motor [voltage_(max)=6V voltage_(min)=3V]  # not connected
  Componente2 = Adafruit TB6612 DC and Stepper Motor Driver [part_number="Adafruit #2448"]
  M8 = DC Motor [voltage_(max)=6V voltage_(min)=3V]  # not connected
  U1 = LM2596 step down module
  U2 = LM2596 step down module

nets:
  N1: A1.Pin_1, Componente2.VCC
  N2: A1.Pin_21, U1.OUT+
  N3: A1.Pin_22, A1.Pin_44, Componente1.-, Componente2.GND, U1.IN-, U1.OUT-, U2.IN-, U2.OUT-
  N4: A1.Pin_26, Componente2.BIN1
  N5: A1.Pin_27, Componente2.BIN2
  N6: A1.Pin_35, Componente2.PWMB
  N7: A1.Pin_36, Componente2.STBY
  N8: A1.Pin_37, Componente2.PWMA
  N9: A1.Pin_38, Componente2.AIN2
  N10: A1.Pin_39, Componente2.AIN1
  N11: Componente1.+, U2.IN+
  N12: Componente2.PWRIN, U2.OUT+

notes:
  LIPO 2S

custom parts:
  ESP32-S3-WROOM-1-N16R8 dev board: ESP32-S3 WIFI+BLE5.0 Development Board ESP32-S3-WROOM-1-N16R8(16M Flash/8SRAM).
  LIPO-2200mAh: 2200mAh Lipo-battery
  Adafruit TB6612 DC and Stepper Motor Driver: Spin two DC motors, step one bi-polar or uni-polar stepper, or fire off two solenoids with 1.2A per channel using the TB6612. These are perhaps better known as "the drivers in our assembled Adafruit Motorshield or Motor HAT." We really like these dual H-bridges, so if you want to control motors without a shield or HAT these are easy to include on any solderless breadboard or perma-proto.
  LM2596 step down module: LM2596 DC-DC step down power supply module 3 A.
