# Fritzing sketch schematics (saved by Fritzing 1.0.5)

parts:
  A2 = ESP32-S3-WROOM-1-N16R8 dev board
  M1 = DC Motor [voltage_(max)=6V voltage_(min)=3V]
  M2 = DC Motor [voltage_(max)=6V voltage_(min)=3V]
  M3 = DC Motor [voltage_(max)=6V voltage_(min)=3V]
  M6 = DC Motor [voltage_(max)=6V voltage_(min)=3V]
  M7 = BTS7960
  M8 = BTS7960
  J2 = Basic Servo
  J3 = Basic Servo
  J4 = Basic Servo
  Componente1 = DC-DC Power Module (5v)
  Componente2 = DC-DC Power Module (5v)
  M4 = DC Motor [voltage_(max)=6V voltage_(min)=3V]
  JP1 = Header 3 [package=screwterminal-3.5mm-3_lock.007s]
  JP2 = Header 3 [package=screwterminal-3.5mm-3_lock.007s]
  M5 = DC Motor [voltage_(max)=6V voltage_(min)=3V]
  J5 = Camdenboss CTB0158-4 [part_number=CTB0158-4 package=THT]
  J6 = Camdenboss CTB0158-4 [part_number=CTB0158-4 package=THT]
  J7 = Camdenboss CTB0158-4 [part_number=CTB0158-4 package=THT]
  J8 = Camdenboss CTB0158-4 [part_number=CTB0158-4 package=THT]
  J9 = Camdenboss CTB0158-5 [part_number=CTB0158-5 package=THT]
  J10 = Camdenboss CTB0158-5 [part_number=CTB0158-5 package=THT]
  J11 = Camdenboss CTB0158-6 [part_number=CTB0158-6 package=THT]
  J12 = Camdenboss CTB0158-4 [part_number=CTB0158-4 package=THT]
  J13 = Camdenboss CTB0158-4 [part_number=CTB0158-4 package=THT]
  J1 = Basic Servo
  JP3 = Header 3 [package=screwterminal-3.5mm-3_lock.007s]
  JP4 = Header 4 [package=screwterminal-3.5mm-4_lock]
  JP5 = Header 4 [package=screwterminal-3.5mm-4_lock]
  JP6 = Header 4 [package=screwterminal-3.5mm-4_lock]
  Componente3 = LIPO-2200mAh
  A3 = ESP32-S3-WROOM-1-N16R8 dev board
  Componente4 = LIPO-2200mAh
  Componente5 = DC-DC Power Module (5v)  # not connected
  Componente6 = DC-DC Power Module (5v)
  JP7 = Header 3 [package=screwterminal-3.5mm-3_lock.007s]  # not connected
  Componente7 = LIPO-2200mAh
  Componente8 = DC-DC Power Module (5v)
  Componente9 = DC-DC Power Module (5v)
  A4 = ESP32-S3-WROOM-1-N16R8 dev board
  J14 = Basic Servo
  J15 = Basic Servo
  J16 = Basic Servo
  J17 = Basic Servo

nets:
  N1: A2.Pin_7, J4.pulse
  N2: A2.Pin_16, M8.pin1
  N3: A2.Pin_17, M8.pin2
  N4: A2.Pin_18, M7.pin1
  N5: A2.Pin_19, M7.pin2
  N6: A2.Pin_21, JP6.3
  N7: A2.Pin_22, A2.Pin_24, A2.Pin_44, J11.pin6, JP3.3
  N8: A2.Pin_35, J3.pulse
  N9: A2.Pin_38, J1.pulse
  N10: A2.Pin_39, J2.pulse
  N11: M1.pin_1, J8.pin2
  N12: M1.pin_2, J7.pin2
  N13: M2.pin_1, J8.pin3
  N14: M2.pin_2, J7.pin3
  N15: M3.pin_1, J8.pin4
  N16: M3.pin_2, J7.pin4
  N17: M6.pin_1, J5.pin1
  N18: M6.pin_2, J6.pin1
  N19: M7.pin3, JP4.4
  N20: M7.pin4, JP4.3
  N21: M7.pin7, JP4.1
  N22: M7.pin8, JP3.1
  N23: M7.pin9, J6.terminal_4
  N24: M7.pin10, J5.pin4
  N25: M7.pin11, JP2.1
  N26: M7.pin12, JP1.1
  N27: M8.pin3, JP5.3
  N28: M8.pin4, JP5.4
  N29: M8.pin7, JP5.2
  N30: M8.pin8, JP3.2
  N31: M8.pin9, J7.pin1
  N32: M8.pin10, J8.pin1
  N33: M8.pin11, JP2.2
  N34: M8.pin12, JP1.2
  N35: J2.gnd, J9.pin2
  N36: J2.vcc, J10.pin2
  N37: J3.gnd, J9.pin3
  N38: J3.vcc, J10.pin4
  N39: J4.gnd, J9.pin4
  N40: J4.vcc, J10.pin5
  N41: Componente1.Vin, J12.pin3
  N42: Componente1.GND, J13.pin2
  N43: Componente1.Vout, JP6.4
  N44: Componente1.GND*, J11.pin2
  N45: Componente2.Vin, J12.pin2
  N46: Componente2.GND, J13.pin1
  N47: Componente2.Vout, J10.pin3
  N48: Componente2.GND*, J11.pin3
  N49: M4.pin_1, J5.pin3
  N50: M4.pin_2, J6.pin3
  N51: JP1.3, J11.pin4
  N52: JP2.3, J12.pin1
  N53: M5.pin_1, J5.pin2
  N54: M5.pin_2, J6.pin2
  N55: J9.pin1, J1.gnd
  N56: J9.pin5, J11.pin5
  N57: J10.pin1, J1.vcc
  N58: J11.pin1, J13.pin3
  N59: J12.terminal_4, Componente3.+
  N60: J13.terminal_4, Componente3.-
  N61: JP4.2, JP6.1
  N62: JP5.1, JP6.2
  N63: A3.Pin_21, Componente6.Vout
  N64: Componente4.+, Componente6.Vin
  N65: Componente4.-, Componente6.GND
  N66: Componente7.+, Componente9.Vin
  N67: Componente7.-, Componente9.GND
  N68: Componente8.Vout, J14.vcc
  N69: Componente9.Vout, A4.Pin_21
  N70: A4.Pin_7, J17.pulse
  N71: A4.Pin_35, J16.pulse
  N72: A4.Pin_38, J14.pulse
  N73: A4.Pin_39, J15.pulse

notes:
  UBEC 5V/3A
  ESP32
  UBEC 6V/8A
  Servos
  12V for DC Motors
  Lipo 3s
  RF
  GPIO 38
  RB
  GPIO 7
  LB
  GPIO 42
  LF
  GPIO 41

custom parts:
  ESP32-S3-WROOM-1-N16R8 dev board: ESP32-S3 WIFI+BLE5.0 Development Board ESP32-S3-WROOM-1-N16R8(16M Flash/8SRAM).
  BTS7960: BTS7960 43A Peak Power H-Bridge PWM Motor Driver
  DC-DC Power Module (5v): DC-DC Power Module based con AMS1117-5.0 Input: DC 6~12V (input power must higher 1V than output power); Output: 5V (+/-0.05V error), 800mA
  LIPO-2200mAh: 2200mAh Lipo-battery
